// Logisim project timed_lab_2a.circ as structural Verilog: 3 circuits, main circuit state machine
module state_machine (
  input  CLK,
  input  H,
  input  RST,
  output W,
  output X,
  output Y,
  output Z
);

  wire _1in, _1out, _2in, _2out, _3in, _3out, _4____5, _4in, _4out, _5____5, _5in, _5out, and_1_out,
       and_2_out, and_3_out, and_4_out, and_5_out, and_6_out, and_7_out, and_8_out, Out5;

  and and_1 (and_1_out, _1out, H);
  or or_1 (_2in, and_1_out, and_2_out);
  and and_2 (and_2_out, _5out, H);
  and and_3 (and_3_out, _2out, ~H);  // AND_Gate
  and and_4 (and_4_out, _4out, ~H);  // AND_Gate
  and and_5 (and_5_out, _5out, ~H);  // AND_Gate
  and and_6 (and_6_out, _2out, H);
  or or_2 (_4in, and_6_out, and_7_out);
  and and_7 (and_7_out, _1out, ~H);  // AND_Gate
  or or_3 (_5in, _3out, and_8_out);
  and and_8 (and_8_out, _4out, H);
  or or_4 (Out5, _4____5, _5____5);
  or or_5 (_3in, and_3_out, and_4_out, and_5_out);
  Register #(.width(5)) register_1 (
    .D({_5in, _4in, _3in, _2in, _1in}), .Q({_5out, _4out, _3out, _2out, _1out}), .clk(CLK), .clr(RST));  // open: en
  nor nor_1 (_1in, _1out, _2out, _3out, _4out, _5out);
  or or_6 (X, _1out, _5out);
  or or_7 (Y, _1out, _2out, _3out, _4out, _5out);
  or or_8 (Z, _3out, _4out);
  or or_9 (W, _2out, _4out);

  // Other names for the same wires on the sheet: start = _1in

  // Notes on the sheet:
  //   Do not place anything here!
  //   Moving the input and output pins of this subcircuit will break the tester subcircuit
  //   Implement your state machine here
endmodule

module one_hot_checker (
);

  wire NEXT_out, one_hot_checker_1_p2, RESET_out, state_machine_1_w, state_machine_1_x, state_machine_1_y,
       state_machine_1_z;

  Clock NEXT (.out(NEXT_out));
  Button RESET (.out(RESET_out));
  // One_Hot_Checker one_hot_checker_1: pin names not known; wires that end beside it: RESET_out, one_hot_checker_1_p2
  state_machine state_machine_1 (
    .CLK(NEXT_out), .H(one_hot_checker_1_p2), .RST(RESET_out), .W(state_machine_1_w), .X(state_machine_1_x),
    .Y(state_machine_1_y), .Z(state_machine_1_z));
endmodule

module reduced_checker (
);

  wire NEXT_out, reduced_checker_1_p2, RESET_out, state_machine_1_w, state_machine_1_x, state_machine_1_y,
       state_machine_1_z;

  Clock NEXT (.out(NEXT_out));
  Button RESET (.out(RESET_out));
  // Reduced_Checker reduced_checker_1: pin names not known; wires that end beside it: RESET_out, reduced_checker_1_p2
  state_machine state_machine_1 (
    .CLK(NEXT_out), .H(reduced_checker_1_p2), .RST(RESET_out), .W(state_machine_1_w), .X(state_machine_1_x),
    .Y(state_machine_1_y), .Z(state_machine_1_z));
endmodule
